# Fritzing sketch 7Seg_RTC (saved by Fritzing 0.9.2b)
circuit board: 8.45183cm x 7.33667cm
breadboards: 1

parts:
  Part1 = Arduino Nano (Rev3.0) (ICSP)
  U1 = 74HC595 [package="DIP16 [THT]"]
  U2 = 7-SEGMENT-4DIGIT [package=7-segment-4digit_longpads_for_pogobed]
  IC1 = ULN2803A [package=THT]
  ZS-042_RTC1 = ZS-042 RTC Module

nets:
  GND: Part1.GND, U1.GND, U1.OE, IC1.0V, ZS-042_RTC1.GND
  N1: Part1.D2, U1.ST_CP
  N2: Part1.D3, U1.DS
  N3: Part1.D4, U1.SH_CP
  N4: Part1.D6, IC1.In_1
  N5: Part1.D7, IC1.In_2
  N6: Part1.D8, IC1.In_3
  N7: Part1.D9, IC1.In_4
  N8: Part1.D10, IC1.In_5
  VCC: Part1.5V, U1.MR, U1.VCC, IC1.COM_-_Common, ZS-042_RTC1.VCC
  N9: Part1.A5, ZS-042_RTC1.SCL
  N10: Part1.A4, ZS-042_RTC1.SDA
  N11: U1.Q1, U2.16
  N12: U1.Q2, U2.13
  N13: U1.Q3, U2.3
  N14: U1.Q4, U2.5
  N15: U1.Q5, U2.11
  N16: U1.Q6, U2.15
  N17: U1.Q7, U2.7
  N18: U1.Q0, U2.14
  N19: U2.1, IC1.Out_1
  N20: U2.2, IC1.Out_2
  N21: U2.4, IC1.Out_5
  N22: U2.6, IC1.Out_3
  N23: U2.8, IC1.Out_4
