# Fritzing sketch 7Seg_displ (saved by Fritzing 0.9.2b)
breadboards: 1

parts:
  Part1 = Arduino Uno (Rev3)
  DI1 = 7-Segment LED Display [package=THT]
  R1 = Resistor [tolerance=±5% resistance=1k package=THT]

nets:
  N1: Part1.D8, DI1.cathodeG
  N2: Part1.D2, DI1.cathodeA
  N3: Part1.D3_PWM, DI1.cathodeB
  N4: Part1.D4, DI1.cathodeC
  N5: Part1.D5_PWM, DI1.cathodeD
  N6: Part1.D6_PWM, DI1.cathodeE
  N7: Part1.D7, DI1.cathodeF
  N8: Part1.GND, R1.Pin_1
  N9: DI1.commAnode#2, R1.Pin_0

// code stored in the sketch: 7Seg_displ.ino
int pinA = 2;
int pinB = 3;
int pinC = 4;
int pinD = 5;
int pinE = 6;
int pinF = 7;
int pinG = 8;

// the setup function runs once when you press reset or power the board
void setup() {
  // initialize digital pin 13 as an output.
  pinMode(pinA, OUTPUT);
  pinMode(pinB, OUTPUT);
  pinMode(pinC, OUTPUT);
  pinMode(pinD, OUTPUT);
  pinMode(pinE, OUTPUT);
  pinMode(pinF, OUTPUT);
  pinMode(pinG, OUTPUT);
}

// the loop function runs over and over again forever
void loop() {
   //9
   digitalWrite(pinA, HIGH);
   digitalWrite(pinB, HIGH);
   digitalWrite(pinC, HIGH);
   digitalWrite(pinD, HIGH);
   digitalWrite(pinE, LOW);
   digitalWrite(pinF, HIGH);
   digitalWrite(pinG, HIGH);
   delay(1000);              // wait for a second
   //8
   digitalWrite(pinA, HIGH);
   digitalWrite(pinB, HIGH);
   digitalWrite(pinC, HIGH);
   digitalWrite(pinD, HIGH);
   digitalWrite(pinE, HIGH);
   digitalWrite(pinF, HIGH);
   digitalWrite(pinG, HIGH);
   delay(1000);
      //7
   digitalWrite(pinA, HIGH);
   digitalWrite(pinB, HIGH);
   digitalWrite(pinC, HIGH);
   digitalWrite(pinD, LOW);
   digitalWrite(pinE, LOW);
   digitalWrite(pinF, LOW);
   digitalWrite(pinG, LOW);
   delay(1000);              // wait for a second
   //6
   digitalWrite(pinA, HIGH);
   digitalWrite(pinB, LOW);
   digitalWrite(pinC, HIGH);
   digitalWrite(pinD, HIGH);
   digitalWrite(pinE, HIGH);
   digitalWrite(pinF, HIGH);
   digitalWrite(pinG, HIGH);
   delay(1000);
   //5
   digitalWrite(pinA, HIGH);
   digitalWrite(pinB, LOW);
   digitalWrite(pinC, HIGH);
   digitalWrite(pinD, HIGH);
   digitalWrite(pinE, LOW);
   digitalWrite(pinF, HIGH);
   digitalWrite(pinG, HIGH);
   delay(1000);
   //4
   digitalWrite(pinA, LOW);
   digitalWrite(pinB, HIGH);
   digitalWrite(pinC, HIGH);
   digitalWrite(pinD, LOW);
   digitalWrite(pinE, LOW);
   digitalWrite(pinF, HIGH);
   digitalWrite(pinG, HIGH);
   delay(1000);
   //3
   digitalWrite(pinA, HIGH);
   digitalWrite(pinB, HIGH);
   digitalWrite(pinC, HIGH);
   digitalWrite(pinD, HIGH);
   digitalWrite(pinE, LOW);
   digitalWrite(pinF, LOW);
   digitalWrite(pinG, HIGH);
   delay(1000);
   //2
   digitalWrite(pinA, HIGH);
   digitalWrite(pinB, HIGH);
   digitalWrite(pinC, LOW);
   digitalWrite(pinD, HIGH);
   digitalWrite(pinE, HIGH);
   digitalWrite(pinF, LOW);
   digitalWrite(pinG, HIGH);
   delay(1000);
   //1
   digitalWrite(pinA, LOW);
   digitalWrite(pinB, HIGH);
   digitalWrite(pinC, HIGH);
   digitalWrite(pinD, LOW);
   digitalWrite(pinE, LOW);
   digitalWrite(pinF, LOW);
   digitalWrite(pinG, LOW);
   delay(1000);
   //0
   digitalWrite(pinA, HIGH);
   digitalWrite(pinB, HIGH);
   digitalWrite(pinC, HIGH);
   digitalWrite(pinD, HIGH);
   digitalWrite(pinE, HIGH);
   digitalWrite(pinF, HIGH);
   digitalWrite(pinG, LOW);
   delay(1000);
}
