# Fritzing sketch ADXL335 (saved by Fritzing 0.9.2b)
breadboards: 1

parts:
  ADXL1 = ADXL335 Accelerometer Breakout
  Part1 = Arduino Uno (Rev3)

nets:
  N1: ADXL1.3Vo, Part1.3V3
  GND: ADXL1.GND, Part1.GND
  N2: ADXL1.Xout, Part1.A3
  N3: ADXL1.Yout, Part1.A4/SDA
  N4: ADXL1.Zout, Part1.A5/SCL

custom parts:
  ADXL335 Accelerometer Breakout: ADXL335 Accelerometer Breakout board

// code stored in the sketch: ADXL335.ino
//Liver u x=123, y=123, z=151

//connect 3.3v to AREF


const int ap1 = A5; 
const int ap2 = A4;
const int ap3 = A3;

int sv1 = 0;        
int ov1 = 0;    
int sv2 = 0;      
int ov2= 0;      
int sv3 = 0;       
int ov3= 0;      

void setup() {
  // initialize serial communications at 9600 bps:
  Serial.begin(9600);
 
}

void loop() {
  analogReference(EXTERNAL);    //connect 3.3v to AREF
  // read the analog in value:
  sv1 = analogRead(ap1);            
  // map it to the range of the analog out:
  ov1 = map(sv1, 0, 1023, 0, 255);  
  // change the analog out value:
  delay(2);                     
  //
  sv2 = analogRead(ap2);            
  
  ov2 = map(sv2, 0, 1023, 0, 255); 
 // 
  delay(2);                 
  //
  sv3 = analogRead(ap3);            
  
  ov3 = map(sv3, 0, 1023, 0, 255);  
  
  // print the results to the serial monitor:
  Serial.print("Xsensor1 = " );                       
  Serial.print(sv1);      
  Serial.print("\t output1 = ");      
  Serial.println(ov1);   
 
  Serial.print("Ysensor2 = " );                       
  Serial.print(sv2);      
  Serial.print("\t output2 = ");      
  Serial.println(ov2);   

  Serial.print("Zsensor3 = " );                       
  Serial.print(sv3);      
  Serial.print("\t output3 = ");      
  Serial.println(ov3);  

  Serial.println("------------------");

  delay(300);                     
  
}
