# Fritzing sketch ESP (saved by Fritzing 0.9.2b)
circuit board: 2.95818cm x 3.02568cm
breadboards: 1

parts:
  IC1 = IC, SIP package, 8 pins [chip_label=IC]
  IC2 = IC, SIP package, 8 pins [chip_label=IC]
  U1 = ESP8266 WiFi Module [part_number=ESP8266]

nets:
  N1: IC1.pin1, U1.TXD
  N2: IC1.pin2, U1.RXD
  N3: IC1.pin3, U1.GPIO_4
  N4: IC1.pin4, U1.GPIO_5
  N5: IC1.pin5, U1.GPIO_0
  N6: IC1.pin6, U1.GPIO_2
  N7: IC1.pin7, U1.GPIO_15
  N8: IC1.pin8, U1.GND
  N9: IC2.pin1, U1.VCC
  N10: IC2.pin2, U1.GPIO_13
  N11: IC2.pin3, U1.GPIO_12
  N12: IC2.pin4, U1.GPIO_14
  N13: IC2.pin5, U1.GPIO_16
  N14: IC2.pin6, U1.CH_PD
  N15: IC2.pin7, U1.ADC_0
  N16: IC2.pin8, U1.REST
