# Fritzing sketch IR led turn on_off (saved by Fritzing 0.9.2b)
breadboards: 1

parts:
  Part1 = Arduino Uno (Rev3)
  IR1 = TSOP312.., 314.. [package=THT]
  R1 = Resistor [tolerance=±5% resistance=220 package=THT]
  LED1 = LED - 5mm [color="Red (633nm)" package="5 mm [THT]"]

nets (from the schematic view):
  N1: Part1.D11_PWM/MOSI, IR1.Data
  GND: Part1.GND, IR1.GND, LED1.cathode
  N2: Part1.D6_PWM, R1.Pin_1
  N3: Part1.5V, IR1.Vs
