# Fritzing sketch IR-remoteRecord (saved by Fritzing 0.9.2b)
breadboards: 1

parts:
  S1 = Momentary Switch [package=ksa_sealed_tac_switch]
  D1 = LTE-302 [package=lte-302]
  IR2 = TSOP382../TSOP384.. [package=THT]
  Part1 = Arduino Uno (Rev3)

nets:
  N1: S1.2, Part1.D12/MISO
  GND: S1.4, D1.C, IR2.GND, Part1.GND
  N2: D1.A, Part1.D3_PWM
  N3: IR2.Data, Part1.D11_PWM/MOSI
  N4: IR2.Vs, Part1.5V

custom parts:
  TSOP382../TSOP384..: The TSOP38#.. series are miniaturized receivers for infrared remote control systems. A PIN diode and a preamplifier are assembled on a lead frame, the epoxy package acts as an IR filter. The demodulated output signal can be directly decoded by a microprocessor. The TSOP382.. is compatible with all common IR remote control data formats. The TSOP384.. is optimized to suppress almost all spurious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

// code stored in the sketch: IR-remoteRecord.ino
/*
 * IRrecord: record and play back IR signals as a minimal 
 * An IR detector/demodulator must be connected to the input RECV_PIN.
 * An IR LED must be connected to the output PWM pin 3.
 * A button must be connected to the input BUTTON_PIN; this is the
 * send button.
 * A visible LED can be connected to STATUS_PIN to provide status.
 *
 * The logic is:
 * If the button is pressed, send the IR code.
 * If an IR code is received, record it.
 *
 * Version 0.11 September, 2009
 * Copyright 2009 Ken Shirriff
 * http://arcfn.com
 */

#include <IRremote.h>

int RECV_PIN = 11;
int BUTTON_PIN = 12;
int STATUS_PIN = 13;

IRrecv irrecv(RECV_PIN);
IRsend irsend;

decode_results results;

void setup()
{
  Serial.begin(9600);
  irrecv.enableIRIn(); // Start the receiver
  pinMode(BUTTON_PIN, INPUT);
  digitalWrite(BUTTON_PIN, HIGH);
  pinMode(STATUS_PIN, OUTPUT);
}

// Storage for the recorded code
int codeType = -1; // The type of code
unsigned long codeValue; // The code value if not raw
unsigned int rawCodes[RAWBUF]; // The durations if raw
int codeLen; // The length of the code
int toggle = 0; // The RC5/6 toggle state

// Stores the code for later playback
// Most of this code is just logging
void storeCode(decode_results *results) {
  codeType = results->decode_type;
  int count = results->rawlen;
  if (codeType == UNKNOWN) {
    Serial.println("Received unknown code, saving as raw");
    codeLen = results->rawlen - 1;
    // To store raw codes:
    // Drop first value (gap)
    // Convert from ticks to microseconds
    // Tweak marks shorter, and spaces longer to cancel out IR receiver distortion
    for (int i = 1; i <= codeLen; i++) {
      if (i % 2) {
        // Mark
        rawCodes[i - 1] = results->rawbuf[i]*USECPERTICK - MARK_EXCESS;
        Serial.print(" m");
      } 
      else {
        // Space
        rawCodes[i - 1] = results->rawbuf[i]*USECPERTICK + MARK_EXCESS;
        Serial.print(" s");
      }
      Serial.print(rawCodes[i - 1], DEC);
    }
    Serial.println("");
  }
  else {
    if (codeType == NEC) {
      Serial.print("Received NEC: ");
      if (results->value == REPEAT) {
        // Don't record a NEC repeat value as that's useless.
        Serial.println("repeat; ignoring.");
        return;
      }
    } 
    else if (codeType == SONY) {
      Serial.print("Received SONY: ");
    } 
    else if (codeType == RC5) {
      Serial.print("Received RC5: ");
    } 
    else if (codeType == RC6) {
      Serial.print("Received RC6: ");
    } 
    else {
      Serial.print("Unexpected codeType ");
      Serial.print(codeType, DEC);
      Serial.println("");
    }
    Serial.println(results->value, HEX);
    codeValue = results->value;
    codeLen = results->bits;
  }
}

void sendCode(int repeat) {
  if (codeType == NEC) {
    if (repeat) {
      irsend.sendNEC(REPEAT, codeLen);
      Serial.println("Sent NEC repeat");
    } 
    else {
      irsend.sendNEC(codeValue, codeLen);
      Serial.print("Sent NEC ");
      Serial.println(codeValue, HEX);
    }
  } 
  else if (codeType == SONY) {
    irsend.sendSony(codeValue, codeLen);
    Serial.print("Sent Sony ");
    Serial.println(codeValue, HEX);
  } 
  else if (codeType == RC5 || codeType == RC6) {
    if (!repeat) {
      // Flip the toggle bit for a new button press
      toggle = 1 - toggle;
    }
    // Put the toggle bit into the code to send
    codeValue = codeValue & ~(1 << (codeLen - 1));
    codeValue = codeValue | (toggle << (codeLen - 1));
    if (codeType == RC5) {
      Serial.print("Sent RC5 ");
      Serial.println(codeValue, HEX);
      irsend.sendRC5(codeValue, codeLen);
    } 
    else {
      irsend.sendRC6(codeValue, codeLen);
      Serial.print("Sent RC6 ");
      Serial.println(codeValue, HEX);
    }
  } 
  else if (codeType == UNKNOWN /* i.e. raw */) {
    // Assume 38 KHz
    irsend.sendRaw(rawCodes, codeLen, 38);
    Serial.println("Sent raw");
  }
}

int lastButtonState;

void loop() {
  // If button pressed, send the code.
  int buttonState = digitalRead(BUTTON_PIN);
  if (lastButtonState == LOW && buttonState == HIGH) {
    Serial.println("Released");
    irrecv.enableIRIn(); // Re-enable receiver
  }

  if (!buttonState) {
    Serial.println("Pressed, sending");
    digitalWrite(STATUS_PIN, HIGH);
    sendCode(lastButtonState == buttonState);
    digitalWrite(STATUS_PIN, LOW);
    delay(50); // Wait a bit between retransmissions
  } 
  else if (irrecv.decode(&results)) {
    digitalWrite(STATUS_PIN, HIGH);
    storeCode(&results);
    irrecv.resume(); // resume receiver
    digitalWrite(STATUS_PIN, LOW);
  }
  lastButtonState = buttonState;
}
