# Fritzing sketch PIR_Motion_Sensor (saved by Fritzing 0.9.2b)
breadboards: 1

parts:
  PIR1 = PIR sensor
  Part1 = Arduino Uno (Rev3)
  R1 = Resistor [tolerance=±5% resistance=220 package=THT]
  LED1 = LED - 5mm [color="Red (633nm)" package="5 mm [THT]"]

nets:
  VDD: PIR1.VDD, Part1.5V
  N1: PIR1.SIG, Part1.D2
  GND: PIR1.GND, Part1.GND, LED1.cathode
  N2: Part1.D12/MISO, R1.Pin_1
  N3: R1.Pin_0, LED1.anode

// code stored in the sketch: PIR_Motion_Sensor.ino
int led = 12;                // the pin that the LED is atteched to
int sensor = 2;              // the pin that the sensor is atteched to
int state = LOW;             // by default, no motion detected
int val = 0;                 // variable to store the sensor status (value)

void setup() {
  pinMode(led, OUTPUT);      // initalize LED as an output
  pinMode(sensor, INPUT);    // initialize sensor as an input
  Serial.begin(9600);        // initialize serial
}

void loop(){
  val = digitalRead(sensor);   // read sensor value
  if (val == HIGH) {           // check if the sensor is HIGH
    digitalWrite(led, HIGH);   // turn LED ON
    delay(100);                // delay 100 milliseconds 
    
    if (state == LOW) {
      Serial.println("Motion detected!"); 
      state = HIGH;       // update variable state to HIGH
    }
  } 
  else {
      digitalWrite(led, LOW); // turn LED OFF
      delay(200);             // delay 200 milliseconds 
      
      if (state == HIGH){
        Serial.println("Motion stopped!");
        state = LOW;       // update variable state to LOW
    }
  }
}
