# Fritzing sketch SR 7Seg (saved by Fritzing 0.9.2b)
breadboards: 1

parts:
  U1 = 74HC595 [package="DIP16 [THT]"]
  7_Segment1 = 7 Segment Display
  Part1 = Arduino Uno (Rev3)
  R1 = Resistor [tolerance=±5% resistance=10k package=THT]

nets:
  N1: U1.Q1, 7_Segment1.Segment_B
  N2: U1.Q2, 7_Segment1.Segment_C
  N3: U1.Q3, 7_Segment1.Segment_D
  N4: U1.Q4, 7_Segment1.Segment_E
  N5: U1.Q5, 7_Segment1.Segment_F
  N6: U1.Q6, 7_Segment1.Segment_G
  GND: U1.GND, U1.OE, Part1.GND, R1.Pin_1
  VCC: U1.MR, U1.VCC, Part1.5V
  N7: U1.SH_CP, Part1.D4
  N8: U1.ST_CP, Part1.D2
  N9: U1.DS, Part1.D3_PWM
  N10: U1.Q0, 7_Segment1.Segment_A
  N11: 7_Segment1.common_cathode, R1.Pin_0
