# Fritzing sketch Spaceship_Interface_MB (saved by Fritzing 0.9.2b)
breadboards: 1

parts:
  Part1 = Arduino Uno (Rev3)
  S1 = Pushbutton [package="[THT]"]
  R1 = Resistor [tolerance=±5% resistance=10k package=THT]
  LED1 = LED - 5mm [color="Green (570nm)" package="5 mm [THT]"]
  LED2 = LED - 5mm [color="Red (633nm)" package="5 mm [THT]"]
  LED3 = LED - 5mm [color="Red (633nm)" package="5 mm [THT]"]
  R2 = Resistor [tolerance=±5% resistance=220 package=THT]
  R3 = Resistor [tolerance=±5% resistance=220 package=THT]
  R4 = Resistor [tolerance=±5% resistance=220 package=THT]

nets:
  N1: Part1.D2, S1.Pin_1, S1.Pin_2, R1.Pin_0
  N2: Part1.D3_PWM, LED1.anode
  N3: Part1.D4, LED2.anode
  N4: Part1.D5_PWM, LED3.anode
  N5: Part1.5V, S1.Pin_3, S1.Pin_4
  N6: Part1.GND, R2.Pin_0, R3.Pin_0, R4.Pin_0
  N7: LED1.cathode, R3.Pin_1
  N8: LED2.cathode, R4.Pin_1
  N9: LED3.cathode, R2.Pin_1

// code stored in the sketch: Spaceship_Interface_MB.ino
boolean onoff = false;
int stanjeSklopke = 0;

void setup() {
  pinMode(2, INPUT);
  pinMode(3, OUTPUT);
  pinMode(4, OUTPUT);
  pinMode(5, OUTPUT);
}

void loop() {
  stanjeSklopke = digitalRead(2);
  
  if(stanjeSklopke == LOW){
  }
  else if(stanjeSklopke == HIGH && onoff == false){
  onoff = true;
  delay(250);
  }
  else if(stanjeSklopke == HIGH && onoff == true){
  onoff = false;
  delay(250);
  }
  
  if(onoff == false){
  digitalWrite(3, HIGH);
  digitalWrite(4, LOW);
  digitalWrite(5, LOW);
  }else{
  digitalWrite(3, LOW);
  digitalWrite(4, LOW);
  digitalWrite(5, HIGH);
  
  delay(100);
  
  digitalWrite(4, HIGH);
  digitalWrite(5, LOW);
  
  delay(100);
  }
}
