# Fritzing sketch Ultrasonic_Led (saved by Fritzing 0.9.2b)
breadboards: 1

parts:
  Part1 = Arduino Uno (Rev3)
  R1 = Resistor [tolerance=±5% resistance=1k package=THT]
  LED1 = LED - 5mm [color="Red (633nm)" package="5 mm [THT]"]
  Part2 = SRF05 Ultrasonic Rangefinder

nets:
  N1: Part1.D8, R1.Pin_1
  N2: Part1.D2, Part2.Echo
  N3: Part1.D3_PWM, Part2.Trig
  5V: Part1.5V, Part2.VCC
  GND: Part1.GND, LED1.cathode, Part2.GND
  N4: R1.Pin_0, LED1.anode

// code stored in the sketch: Ultrasonic_Led.ino
#define echoPin 2
#define trigPin 3
#define led 8

void setup() {
  Serial.begin(9600);
  pinMode(trigPin, OUTPUT);
  pinMode(echoPin, INPUT);
  pinMode(led, OUTPUT);
  
}

void loop() {
  // put your main code here, to run repeatedly:
  int udaljenost, vrijeme;
  digitalWrite(trigPin, HIGH);
  delayMicroseconds(1000);
  digitalWrite(trigPin, LOW);
  vrijeme = pulseIn(echoPin, HIGH);
  udaljenost = (vrijeme/2) / 29.1;
  if(udaljenost<=10){
  digitalWrite(led, HIGH);
  }
  else{
  digitalWrite(led, LOW);
  }
  Serial.print(udaljenost);
  Serial.print(" cm\n");
  delay(500);

}
