# Fritzing sketch nRF24_rec (saved by Fritzing 0.9.2b)
breadboards: 1

parts:
  Part1 = NRF24L01+ Breakout Board
  C1 = Capacitor Polarized [package=cpol-radial-10uf-25v]
  Part2 = Arduino Uno (Rev3)
  LED1 = LED - 5mm [color="Red (633nm)" package="5 mm [THT]"]
  R1 = Resistor [tolerance=±5% resistance=220 package=THT]

nets:
  N1: Part1.GND, C1.-
  VCC: Part1.VCC, C1.+, Part2.3V3
  N2: Part1.CE, Part2.D9_PWM
  N3: Part1.CS, Part2.D10_PWM/SS
  N4: Part1.SCK, Part2.D13/SCK
  N5: Part1.MOSI, Part2.D11_PWM/MOSI
  N6: Part1.MISO, Part2.D12/MISO
  N7: Part2.D3_PWM, R1.Pin_1
  N8: Part2.GND, LED1.cathode
  N9: LED1.anode, R1.Pin_0

// code stored in the sketch: nRF24_rec.ino
#include <SPI.h>
#include "RF24.h"
int msg[1];
RF24 radio(9,10);
const uint64_t pipe = 0xE8E8F0F0E1LL;
int LED1 = 3;

void setup(void){
 Serial.begin(9600);
 radio.begin();
 radio.openReadingPipe(1,pipe);
 radio.startListening();
 pinMode(LED1, OUTPUT);}

void loop(void){
 if (radio.available()){
     radio.read(msg, 1);     
     Serial.println(msg[0]);
     if (msg[0] == 111){
      delay(10);
      digitalWrite(LED1, HIGH);
      }
     else {
      digitalWrite(LED1, LOW);
     }
     delay(10);
     }
     else{
      Serial.println("No radio available");
     }
  }

// code stored in the sketch: nRF24_trans.ino
#include <SPI.h>
#include "RF24.h"
int msg[1];
RF24 radio(9,10);
const uint64_t pipe = 0xE8E8F0F0E1LL;
int LED1 = 3;

void setup(void){
 Serial.begin(9600);
 radio.begin();
 radio.openReadingPipe(1,pipe);
 radio.startListening();
 pinMode(LED1, OUTPUT);}

void loop(void){
 if (radio.available()){
     radio.read(msg, 1);     
     Serial.println(msg[0]);
     if (msg[0] == 111){
      delay(10);
      digitalWrite(LED1, HIGH);
      }
     else {
      digitalWrite(LED1, LOW);
     }
     delay(10);
     }
     else{
      Serial.println("No radio available");
     }
  }
