# Fritzing sketch nRF24_trans (saved by Fritzing 0.9.2b)
breadboards: 1

parts:
  Part1 = NRF24L01+ Breakout Board
  C1 = Capacitor Polarized [package=cpol-radial-10uf-25v]
  Part2 = Arduino Uno (Rev3)
  S1 = Pushbutton [package="[THT]"]
  R1 = Resistor [tolerance=±5% resistance=10k package=THT]

nets:
  N1: Part1.GND, C1.-
  VCC: Part1.VCC, C1.+, Part2.3V3
  N2: Part1.CE, Part2.D9_PWM
  N3: Part1.CS, Part2.D10_PWM/SS
  N4: Part1.SCK, Part2.D13/SCK
  N5: Part1.MOSI, Part2.D11_PWM/MOSI
  N6: Part1.MISO, Part2.D12/MISO
  N7: Part2.D7, S1.Pin_1, S1.Pin_2, R1.Pin_0
  N8: Part2.5V, S1.Pin_3, S1.Pin_4
  N9: Part2.GND, R1.Pin_1

// code stored in the sketch: nRF24_trans.ino
#include  <SPI.h>
#include "RF24.h"
int msg[1];
RF24 radio(9,10);
const uint64_t pipe = 0xE8E8F0F0E1LL;
int SW1 = 7;

void setup(void){
 Serial.begin(9600);
 radio.begin();
 radio.openWritingPipe(pipe);
 pinMode(SW1, INPUT);
 }

void loop(void){
 if (digitalRead(SW1) == HIGH){
 msg[0] = 111;
 radio.write(msg, 1);
 Serial.println("Button pressed!");
 }
 else{
  msg[0] = 000;
  radio.write(msg, 1);
  }
 
 }
